# Fritzing sketch diagram (saved by Fritzing 0.9.3b)

parts:
  U1 = NodeMCU V1.0
  Part1 = MQ-3 breakout
  J1 = Piezo Speaker
  LED1 = LEDs [package=led10mm]
  R1 = Resistor [tolerance=±5% resistance=220 package="0805 [SMD]"]
  Mod1 = KY-026 Flame Sensor Module [package="Breakout board"]
  Mod2 = KY-026 Flame Sensor Module [package="Breakout board"]
  Mod3 = KY-015 Temperature & Humidity Sensor Module [package="Breakout board"]

nets:
  N1: U1.D1, Mod1.D0, Mod2.D0
  N2: U1.D3, Mod3.Vin
  3V3: U1.3V3, Part1.VCC, Mod1.+, Mod2.+, Mod3.S
  GND: U1.GND, Part1.GND, J1.pin1, LED1.C, Mod1.G, Mod2.G, Mod3.-
  N3: U1.D5, R1.Pin_0
  N4: U1.D6, J1.pin2
  N5: U1.A0, Part1.AO
  N6: LED1.A, R1.Pin_1

custom parts:
  NodeMCU V1.0: ESP8266 based NodeMCU
  MQ-3 breakout: Alcohol sensor is capable of detecting alcohol (ethanol) particles on itself and gives the information in digital form back to us to manipulate with it. SKU:101251 • Voltage: 5V DC • Power: max 750mW • Measurement range: 0.04-4mg/L
  KY-026 Flame Sensor Module: KY-026 Flame Sensor Module reacts in the presence of fire.
  KY-015 Temperature & Humidity Sensor Module: KY-015 temperature and humidity sensor module, provides a low-latency serial interface to measure humidity and temperature.
